# Fritzing sketch Diagram (saved by Fritzing 0.9.10b)
circuit board: 8.46667cm x 5.64444cm
stripboards: 2

parts:
  WeMos_D1_Mini1 = WeMos D1 Mini
  J1 = Power Jack [package=power_jack_smd]
  M1 = RioRand LM2596
  Q1 = Basic FET N-Channel [package="DPak [SMD]"]
  R1 = Resistor [tolerance=±5% resistance=10k package="0402 [SMD]"]
  Q2 = Basic FET N-Channel [package="DPak [SMD]"]
  Q3 = Basic FET N-Channel [package="DPak [SMD]"]
  R2 = Resistor [tolerance=±5% resistance=10k package="0402 [SMD]"]
  R3 = Resistor [tolerance=±5% resistance=10k package="0402 [SMD]"]
  RHT1 = Humidity and Temperature Sensor RHT03
  R4 = Resistor [tolerance=±5% resistance=220 package="0402 [SMD]"]
  OLED1 = OLED 128x64 I2C Monochrome Display
  RGB_Strip_LED1 = RGB Strip LED
  RGB_Strip_LED2 = RGB Strip LED

nets (from the breadboard view):
  3V3: WeMos_D1_Mini1.3V3, OLED1.VDD
  5V: WeMos_D1_Mini1.5V, M1.Pin_3, RHT1.Vcc, R4.Pin_0
  N1: WeMos_D1_Mini1.D1, OLED1.SCK
  N2: WeMos_D1_Mini1.D2, OLED1.SDA
  N3: WeMos_D1_Mini1.D4, R4.Pin_1
  N4: WeMos_D1_Mini1.D5, Q1.Gate, R1.Pin_1
  N5: WeMos_D1_Mini1.D6, R2.Pin_1
  N6: WeMos_D1_Mini1.D7, R3.Pin_1
  N7: WeMos_D1_Mini1.G, M1.Pin_4, R1.Pin_0, R2.Pin_0, R3.Pin_0, RHT1.GND_2, OLED1.GND
  N8: J1.GND, M1.Pin_2, Q1.source, Q2.source, Q3.drain, Q3.source, RGB_Strip_LED1.Blue_Connect#11
  N9: J1.GNDBREAK, M1.Pin_1, RGB_Strip_LED1.Common_Connect#8
  N10: Q1.drain, RGB_Strip_LED1.Red_Connect#10
  N11: Q2.drain, RGB_Strip_LED1.Green_Connect#9
  N12: RGB_Strip_LED1.Common_Connect#12, RGB_Strip_LED2.Common_Connect
  N13: RGB_Strip_LED1.Green_Connect#13, RGB_Strip_LED2.Green_Connect
  N14: RGB_Strip_LED1.Red_Connect#14, RGB_Strip_LED2.Red_Connect
  N15: RGB_Strip_LED1.Blue_Connect#15, RGB_Strip_LED2.Blue_Connect

notes:
  12v
  5v

custom parts:
  RGB Strip LED: A tri-color Strip LED with red, green and blue. Based on LED SMD 5050 RGB Pin order: common cathode - green - red - blue
